// Logisim project REGISTRADOR-MULTI.circ as structural Verilog: 1 circuit, main circuit main
module main (
  input  A0,
  input  A1,
  input  A2,
  input  A3,
  input  enable,
  input  CLEAR,
  input  CLOCK
);

  wire I0, I1, I2, I3;
  wire [2:0] undriven;

  and and_1 (I0, enable, A0);
  and and_2 (I1, enable, A1);
  and and_3 (I2, enable, A2);
  and and_4 (I3, enable, A3);
  Multiplexer #(.select(3)) multiplexer_1 (
    .in0(I0), .sel(undriven));  // open: in1, in2, in3, in4, in5, in6, in7, out, en
  D_Flip_Flop d_ff_1 (.clk(CLOCK), .reset(CLEAR));  // open: D, Q, Qn, preset, en
  D_Flip_Flop d_ff_2 (.clk(CLOCK), .reset(CLEAR));  // open: D, Q, Qn, preset, en
  Multiplexer #(.select(3)) multiplexer_2 (
    .in0(I1), .sel(undriven));  // open: in1, in2, in3, in4, in5, in6, in7, out, en
  D_Flip_Flop d_ff_3 (.clk(CLOCK), .reset(CLEAR));  // open: D, Q, Qn, preset, en
  Multiplexer #(.select(3)) multiplexer_3 (
    .in0(I2), .sel(undriven));  // open: in1, in2, in3, in4, in5, in6, in7, out, en
  D_Flip_Flop d_ff_4 (.clk(CLOCK), .reset(CLEAR));  // open: D, Q, Qn, preset, en
  Multiplexer #(.select(3)) multiplexer_4 (
    .in0(I3), .sel(undriven));  // open: in1, in2, in3, in4, in5, in6, in7, out, en
endmodule
