// Logisim project sinalizador luminoso.circ as structural Verilog: 1 circuit, main circuit main
module main (
  input  A,
  input  B,
  input  C,
  input  D,
  input  E,
  input  Clear,
  input  ENABLE
);

  wire A_q, A_qn, and_1_out, and_2_out, and_3_out, and_4_out, and_5_out, AND_Ja_2_out, AND_Ja_out,
       AND_Jc_out, AND_Jd_out, AND_Je_out, AND_Ke_out, B_q, B_qn, C_q, C_qn, clock_1_out, D_q, D_qn, E_q,
       E_qn, OR_Ja_out, OR_Jc_out, OR_Ka_out, OR_Kb_out, OR_Kc_out, XNOR_Jb_out;

  and and_1 (and_1_out, A, ENABLE);
  and and_2 (and_2_out, B, ENABLE);
  and and_3 (and_3_out, C, ENABLE);
  and and_4 (and_4_out, D, ENABLE);
  and and_5 (and_5_out, E, ENABLE);
  xnor XNOR_Jb (XNOR_Jb_out, D_q, C_q);
  J_K_Flip_Flop u_A (
    .J(OR_Ja_out), .clk(clock_1_out), .K(OR_Ka_out), .Q(A_q), .Qn(A_qn), .preset(and_1_out), .reset(Clear));  // open: en
  or OR_Kb (OR_Kb_out, C_qn, E_q);
  LED led_1 (.in(A_q));
  or OR_Ka (OR_Ka_out, B_qn, E_q);
  or OR_Jc (OR_Jc_out, E_q, AND_Jc_out);
  or OR_Ja (OR_Ja_out, AND_Ja_out, AND_Ja_2_out);
  or OR_Kc (OR_Kc_out, D_qn, B_q);
  J_K_Flip_Flop u_B (
    .J(XNOR_Jb_out), .clk(clock_1_out), .K(OR_Kb_out), .Q(B_q), .Qn(B_qn), .preset(and_2_out), .reset(Clear));  // open: en
  and AND_Jc (AND_Jc_out, D_qn, A_qn);
  LED led_2 (.in(B_q));
  and AND_Jd (AND_Jd_out, A_qn, B_qn);
  J_K_Flip_Flop u_C (
    .J(OR_Jc_out), .clk(clock_1_out), .K(OR_Kc_out), .Q(C_q), .Qn(C_qn), .preset(and_3_out), .reset(Clear));  // open: en
  LED led_3 (.in(C_q));
  and AND_Ja (AND_Ja_out, B_q, C_q);
  and AND_Ja_2 (AND_Ja_2_out, D_qn, E_q);
  J_K_Flip_Flop u_D (
    .J(AND_Jd_out), .clk(clock_1_out), .K(E_qn), .Q(D_q), .Qn(D_qn), .preset(and_4_out), .reset(Clear));  // open: en
  LED led_4 (.in(D_q));
  and AND_Ke (AND_Ke_out, A_qn, D_q);
  and AND_Je (AND_Je_out, AND_Jd_out, C_qn);
  J_K_Flip_Flop u_E (
    .J(AND_Je_out), .clk(clock_1_out), .K(AND_Ke_out), .Q(E_q), .Qn(E_qn), .preset(and_5_out), .reset(Clear));  // open: en
  LED led_5 (.in(E_q));
  Clock clock_1 (.out(clock_1_out));
endmodule
