// Logisim project Maquina de Estados.circ as structural Verilog: 1 circuit, main circuit main
module main (
  input  D
);

  wire _0_q, _0_qn, _1_q, _1_qn, and_1_out, and_2_out, and_3_out, clock_1_out, Clr_out, Go_out, J1_out,
       K0_out, K1_out, LD_out, not_1_out, not_2_out, xor_1_out;

  Clock clock_1 (.out(clock_1_out));
  Button LD (.out(LD_out));
  Button Go (.out(Go_out));
  not not_1 (not_1_out, Go_out);
  LED led_1 (.in(_1_q));
  J_K_Flip_Flop _1 (
    .J(J1_out), .clk(clock_1_out), .K(K1_out), .Q(_1_q), .Qn(_1_qn), .en(1'b1), .reset(Clr_out));  // open: preset
  xor xor_1 (xor_1_out, Go_out, LD_out);
  or K1 (K1_out, _0_qn, not_2_out);
  LED LD_R (.in(_1_qn));
  and and_1 (and_1_out, LD_out, not_1_out);
  and J1 (J1_out, xor_1_out, _0_q);
  and K0 (K0_out, and_1_out, _1_qn);
  LED led_2 (.in(_0_q));
  J_K_Flip_Flop _0 (
    .J(1'b1), .clk(clock_1_out), .K(K0_out), .Q(_0_q), .Qn(_0_qn), .en(1'b1), .reset(Clr_out));  // open: preset
  Button Clr (.out(Clr_out));
  and and_2 (and_2_out, _1_qn, _0_qn);
  LED CLR_2 (.in(and_2_out));
  and and_3 (and_3_out, _0_qn, _1_q);
  LED STACK (.in(and_3_out));
  not not_2 (not_2_out, D);
endmodule
