// Logisim project PROJETO TERCEIRA UNIDADE.circ as structural Verilog: 1 circuit, main circuit main
module main (
  input  in_1,
  input  in_2,
  input  in_3,
  input  in_4,
  input  LD,
  input  CLEAR,
  output [3:0] out_7,
  output [3:0] out_8,
  output [3:0] out_9
);

  wire C1, C2, C3, CLOCK_out, M_A0, M_A1, M_B0, M_B1, not_1_out, not_2_out;
  wire [3:0] DA, DB, DC;

  and and_1 (M_A1, C1, C2);
  and and_2 (M_A0, C1, not_1_out);
  not not_1 (not_1_out, C2);
  Clock CLOCK (.out(CLOCK_out));
  Register #(.width(4)) REG_A (.D(DA), .en(LD), .Q(out_7), .clk(CLOCK_out), .clr(CLEAR));
  Multiplexer #(.select(2), .width(4)) multiplexer_1 (
    .in0(out_7), .in1(out_8), .in2(out_9), .in3({in_4, in_3, in_2, in_1}), .out(DA), .sel({M_A1, M_A0}));  // open: en
  not not_2 (not_2_out, C1);
  and and_3 (M_B1, not_2_out, C2);
  xor xor_1 (M_B0, C1, C2);
  Register #(.width(4)) REG_B (.D(DB), .en(LD), .Q(out_8), .clk(CLOCK_out), .clr(CLEAR));
  Multiplexer #(.select(2), .width(4)) multiplexer_2 (
    .in0(out_7), .in1(out_8), .in2(out_9), .in3(out_7), .out(DB), .sel({M_B1, M_B0}));  // open: en
  Register #(.width(4)) REG_C (.D(DC), .en(LD), .Q(out_9), .clk(CLOCK_out), .clr(CLEAR));
  Comparator #(.width(4)) comparator_1 (.a(out_7), .b(out_8), .lt(C1));  // open: gt, eq
  Multiplexer #(.select(2), .width(4)) multiplexer_3 (
    .in0(out_7), .in1(out_8), .in2(out_9), .in3(out_8), .out(DC), .sel({C2, M_B1}));  // open: en
  Comparator #(.width(4)) comparator_2 (.a(out_8), .b(out_9), .lt(C2));  // open: gt, eq
  Comparator #(.width(4)) comparator_3 (.a(out_7), .b(out_9), .lt(C3));  // open: gt, eq

  // Other names for the same wires on the sheet: M_C0 = M_B1; M_C1 = C2; SA[3:0] = out_7; SB[3:0] = out_8;
  //   SC[3:0] = out_9
endmodule
